# Fritzing sketch Sensor pH (saved by Fritzing 0.9.3b)

parts:
  M1 = PH meter with sensor in breadboard [package=THT]
  Part2 = Arduino Board Ethernet

nets:
  N1: M1.pin1, Part2.A0
  N2: M1.pin2, Part2.5V
  N3: M1.pin3, Part2.GND

custom parts:
  PH meter with sensor in breadboard: DFrobot PH meter (SKU SEN0161)
